# Fritzing sketch digitalVoltmeter (saved by Fritzing 0.9.3b)
breadboards: 1

parts:
  7SEG3 = 7-Segment LED I2C Backpack (white)
  Part1 = Arduino Uno (Rev3) - ICSP
  R1 = Resistor [tolerance=±5% resistance=30k package=THT]
  R2 = Resistor [tolerance=±5% resistance=10k package=THT]

nets:
  N1: 7SEG3.V+, Part1.5V
  GND: 7SEG3.GND, Part1.GND, R1.Pin_0
  N2: 7SEG3.SDA, Part1.A4/SDA
  N3: 7SEG3.SCL, Part1.A5/SCL
  N4: Part1.A0, R1.Pin_1, R2.Pin_0

notes:
  Test here

custom parts:
  7-Segment LED I2C Backpack (white): 4-digit, 7-segment LED Display with I2C Control
